# Fritzing sketch RFID (saved by Fritzing 0.9.7b)
breadboards: 1

parts:
  Mod1 = Raspberry Pi 4B
  Componente1 = RFID-RC522-v3
  LED1 = LED - 3mm [color="Red (633nm)" current=0.030 package="3 mm [THT]"]
  LED2 = LED - 3mm [color="Green (555nm)" current=0.030 package="3 mm [THT]"]
  R1 = Resistor [tolerance=±5% power=0.25 resistance=220 package=THT]
  R2 = Resistor [tolerance=±5% power=0.25 resistance=220 package=THT]

nets:
  3V3: Mod1.3V3, Componente1.3.3V
  GND: Mod1.GND, Componente1.GND, LED1.cathode, LED2.cathode
  N1: Mod1.GPIO14, R1.Pin_0
  N2: Mod1.GPIO15, R2.Pin_0
  N3: Mod1.GPIO10, Componente1.MOSI
  N4: Mod1.GPIO9, Componente1.MISO
  N5: Mod1.GPIO25, Componente1.RST
  N6: Mod1.GPIO11, Componente1.SCK
  N7: Mod1.GPIO8, Componente1.SDA
  N8: LED1.anode, R1.Pin_1
  N9: LED2.anode, R2.Pin_1

custom parts:
  RFID-RC522-v3: A simple China made RFID-RC522 Reader (6x4 cm); do check the pin labels, as this is a MFRC522 based clone.
